// Logisim project Calculator.circ as structural Verilog: 1 circuit, main circuit main
// .
module main (
);

  wire _00, _01, _02, _03, _04, _05, _06, _07, _08, _09, A, AC, and_1_out, and_2_out, B, C,
       controlled_buffer_41_out, controlled_buffer_42_out, D, Divide, E, F, LED1, LED2, Minus, NEXT,
       not_1_out, not_2_out, not_3_out, ON, or_1_out, or_2_out, or_3_out, or_4_out, or_5_out, or_6_out,
       or_7_out, or_8_out, or_9_out, or_10_out, or_11_out, or_12_out, or_13_out, or_14_out, or_15_out,
       or_16_out, or_17_out, or_18_out, or_19_out, or_20_out, or_21_out, or_22_out, or_23_out, or_24_out,
       or_25_out, or_26_out, or_27_out, or_28_out, or_29_out, or_30_out, or_31_out, or_32_out, or_33_out,
       or_34_out, or_35_out, or_36_out, Plus, TImes, tunnel_t_t_t_t;
  wire [3:0] controlled_buffer_1_out, D1, D2, D3, D4, D5, D6, D7, D8;
  wire [4:0] controlled_buffer_7_out, controlled_buffer_8_out, controlled_buffer_9_out,
       controlled_buffer_10_out, controlled_buffer_11_out, controlled_buffer_26_out,
       controlled_buffer_27_out, controlled_buffer_28_out, controlled_buffer_29_out,
       controlled_buffer_30_out, controlled_buffer_31_out, controlled_buffer_32_out,
       controlled_buffer_33_out, controlled_buffer_34_out, controlled_buffer_35_out,
       controlled_buffer_36_out, controlled_buffer_37_out, controlled_buffer_38_out,
       controlled_buffer_39_out, controlled_buffer_40_out, controlled_buffer_43_out,
       controlled_buffer_44_out, controlled_buffer_45_out, controlled_buffer_46_out,
       controlled_buffer_47_out, Di1, Di2, Di3, Di4, Di5, E1, E2, E3, E4, E5, M1, M2, M3, M4, M5, P1, P2, P3,
       P4, P5, S1, S2, S3, S4, S5, T1, T2, T3, T4, T5;
  wire [31:0] _1, _2, adder_1_out, controlled_buffer_6_out, divider_1_out, multiplier_1_out, register_6_q,
       subtractor_1_out;

  Hex_Digit_Display hex_digit_display_1 (.value(_1[31:28]));  // open: dp
  LED led_1 (.in(LED1));
  Hex_Digit_Display hex_digit_display_2 (.value(_1[27:24]));  // open: dp
  Hex_Digit_Display hex_digit_display_3 (.value(_1[23:20]));  // open: dp
  assign controlled_buffer_1_out = _01 ? 4'b0001 : 4'bz;  // Controlled_Buffer controlled_buffer_1
  assign controlled_buffer_1_out = _04 ? 4'b0100 : 4'bz;  // Controlled_Buffer controlled_buffer_2
  assign controlled_buffer_1_out = _07 ? 4'b0111 : 4'bz;  // Controlled_Buffer controlled_buffer_3
  assign controlled_buffer_1_out = A ? 4'b1010 : 4'bz;  // Controlled_Buffer controlled_buffer_4
  assign controlled_buffer_1_out = D ? 4'b1101 : 4'bz;  // Controlled_Buffer controlled_buffer_5
  Adder #(.width(32)) adder_1 (.a(_1), .b(_2), .out(adder_1_out));  // open: cin, cout
  assign controlled_buffer_6_out = Plus ? adder_1_out : 32'bz;  // Controlled_Buffer controlled_buffer_6
  Subtractor #(.width(32)) subtractor_1 (.a(_1), .b(_2), .out(subtractor_1_out));  // open: bin, bout
  Multiplier #(.width(32)) multiplier_1 (.a(_1), .b(_2), .out(multiplier_1_out));  // open: cin, cout
  Divider #(.width(32)) divider_1 (.a(_1), .b(_2), .out(divider_1_out));  // open: upper, rem
  assign controlled_buffer_7_out = Plus ? 5'b00100 : 5'bz;  // Controlled_Buffer controlled_buffer_7
  assign controlled_buffer_8_out = Plus ? 5'b00100 : 5'bz;  // Controlled_Buffer controlled_buffer_8
  assign controlled_buffer_9_out = Plus ? {5{1'b1}} : 5'bz;  // Controlled_Buffer controlled_buffer_9
  assign controlled_buffer_10_out = Plus ? 5'b00100 : 5'bz;  // Controlled_Buffer controlled_buffer_10
  assign controlled_buffer_11_out = Plus ? 5'b00100 : 5'bz;  // Controlled_Buffer controlled_buffer_11
  Hex_Digit_Display hex_digit_display_4 (.value(_1[19:16]));  // open: dp
  Hex_Digit_Display hex_digit_display_5 (.value(_1[15:12]));  // open: dp
  assign controlled_buffer_1_out = _02 ? 4'b0010 : 4'bz;  // Controlled_Buffer controlled_buffer_12
  assign controlled_buffer_1_out = _05 ? 4'b0101 : 4'bz;  // Controlled_Buffer controlled_buffer_13
  assign controlled_buffer_1_out = _08 ? 4'b1000 : 4'bz;  // Controlled_Buffer controlled_buffer_14
  assign controlled_buffer_1_out = B ? 4'b1011 : 4'bz;  // Controlled_Buffer controlled_buffer_15
  assign controlled_buffer_1_out = E ? 4'b1110 : 4'bz;  // Controlled_Buffer controlled_buffer_16
  assign controlled_buffer_1_out = _00 ? 4'b0000 : 4'bz;  // Controlled_Buffer controlled_buffer_17
  assign controlled_buffer_6_out = Minus ? subtractor_1_out : 32'bz;  // Controlled_Buffer controlled_buffer_18
  assign controlled_buffer_6_out = TImes ? multiplier_1_out : 32'bz;  // Controlled_Buffer controlled_buffer_19
  assign controlled_buffer_6_out = Divide ? divider_1_out : 32'bz;  // Controlled_Buffer controlled_buffer_20
  Register #(.width(5)) register_1 (.D(controlled_buffer_7_out), .Q(P1), .clk(or_1_out), .clr(or_6_out));  // open: en
  or or_1 (or_1_out, Plus, Plus);
  Register #(.width(5)) register_2 (.D(controlled_buffer_8_out), .Q(P2), .clk(or_2_out), .clr(or_6_out));  // open: en
  or or_2 (or_2_out, Plus, Plus);
  Register #(.width(5)) register_3 (.D(controlled_buffer_9_out), .Q(P3), .clk(or_3_out), .clr(or_6_out));  // open: en
  or or_3 (or_3_out, Plus, Plus);
  Register #(.width(5)) register_4 (.D(controlled_buffer_10_out), .Q(P4), .clk(or_4_out), .clr(or_6_out));  // open: en
  or or_4 (or_4_out, Plus, Plus);
  Register #(.width(5)) register_5 (.D(controlled_buffer_11_out), .Q(P5), .clk(or_5_out), .clr(or_6_out));  // open: en
  or or_5 (or_5_out, Plus, Plus);
  Hex_Digit_Display hex_digit_display_6 (.value(_1[11:8]));  // open: dp
  Hex_Digit_Display hex_digit_display_7 (.value(_1[7:4]));  // open: dp
  assign controlled_buffer_1_out = _03 ? 4'b0011 : 4'bz;  // Controlled_Buffer controlled_buffer_21
  assign controlled_buffer_1_out = _06 ? 4'b0110 : 4'bz;  // Controlled_Buffer controlled_buffer_22
  assign controlled_buffer_1_out = _09 ? 4'b1001 : 4'bz;  // Controlled_Buffer controlled_buffer_23
  assign controlled_buffer_1_out = C ? 4'b1100 : 4'bz;  // Controlled_Buffer controlled_buffer_24
  assign controlled_buffer_1_out = F ? 4'b1111 : 4'bz;  // Controlled_Buffer controlled_buffer_25
  or or_6 (or_6_out, AC, or_7_out);
  or or_7 (or_7_out, Minus, TImes, Divide);
  DotMatrix #(.matrixrows(5)) dotmatrix_1 (.col0(S1), .col1(S2), .col2(S3), .col3(S4), .col4(S5));
  Hex_Digit_Display hex_digit_display_8 (.value(_1[3:0]));  // open: dp
  Register #(.width(32)) register_6 (
    .D(controlled_buffer_6_out), .Q(register_6_q), .clk(or_8_out), .clr(AC));  // open: en
  or or_8 (or_8_out, Plus, Minus, TImes, Divide);
  assign controlled_buffer_26_out = Minus ? 5'b00100 : 5'bz;  // Controlled_Buffer controlled_buffer_26
  assign controlled_buffer_27_out = Minus ? 5'b00100 : 5'bz;  // Controlled_Buffer controlled_buffer_27
  assign controlled_buffer_28_out = Minus ? 5'b00100 : 5'bz;  // Controlled_Buffer controlled_buffer_28
  assign controlled_buffer_29_out = Minus ? 5'b00100 : 5'bz;  // Controlled_Buffer controlled_buffer_29
  assign controlled_buffer_30_out = Minus ? 5'b00100 : 5'bz;  // Controlled_Buffer controlled_buffer_30
  LED led_2 (.in(LED2));
  Hex_Digit_Display hex_digit_display_9 (.value(_2[27:24]));  // open: dp
  Hex_Digit_Display hex_digit_display_10 (.value(_2[31:28]));  // open: dp
  LED led_3 (.in(LED1));
  // Probe on _1
  DotMatrix #(.matrixrows(5)) dotmatrix_2 (.col0(S1), .col1(S2), .col2(S3), .col3(S4), .col4(S5));
  Button button (.out(NEXT));
  Button u__1 (.out(_01));
  Button _4 (.out(_04));
  Button _7 (.out(_07));
  Button u_AC (.out(AC));
  or or_9 (or_9_out, _01, _02, _03, _04, _05, _06, _07, _08, _09, A, B, C, D, E, F, _00);
  Register #(.width(5)) register_7 (
    .D(controlled_buffer_26_out), .Q(M1), .clk(or_10_out), .clr(or_15_out));  // open: en
  or or_10 (or_10_out, Minus, Minus);
  Register #(.width(5)) register_8 (
    .D(controlled_buffer_27_out), .Q(M2), .clk(or_11_out), .clr(or_15_out));  // open: en
  or or_11 (or_11_out, Minus, Minus);
  Register #(.width(5)) register_9 (
    .D(controlled_buffer_28_out), .Q(M3), .clk(or_12_out), .clr(or_15_out));  // open: en
  or or_12 (or_12_out, Minus, Minus);
  Register #(.width(5)) register_10 (
    .D(controlled_buffer_29_out), .Q(M4), .clk(or_13_out), .clr(or_15_out));  // open: en
  or or_13 (or_13_out, Minus, Minus);
  Register #(.width(5)) register_11 (
    .D(controlled_buffer_30_out), .Q(M5), .clk(or_14_out), .clr(or_15_out));  // open: en
  or or_14 (or_14_out, Minus, Minus);
  Hex_Digit_Display hex_digit_display_11 (.value(_2[23:20]));  // open: dp
  Hex_Digit_Display hex_digit_display_12 (.value(_2[19:16]));  // open: dp
  Button _3 (.out(_03));
  Button u__2 (.out(_02));
  Button _6 (.out(_06));
  Button _5 (.out(_05));
  Button _9 (.out(_09));
  Button _8 (.out(_08));
  Button button_2 (.out(tunnel_t_t_t_t));
  Button _0 (.out(_00));
  Register #(.width(32)) register_12 (
    .D(register_6_q), .Q({D1, D2, D3, D4, D5, D6, D7, D8}), .clk(tunnel_t_t_t_t), .clr(AC));  // open: en
  or or_15 (or_15_out, AC, or_16_out);
  or or_16 (or_16_out, Plus, TImes, Divide);
  Hex_Digit_Display hex_digit_display_13 (.value(_2[11:8]));  // open: dp
  Hex_Digit_Display hex_digit_display_14 (.value(_2[15:12]));  // open: dp
  LED led_4 (.in(LED2));
  // Probe on _2
  DotMatrix #(.matrixrows(5)) dotmatrix_3 (.col0(E1), .col1(E2), .col2(E3), .col3(E4), .col4(E5));
  Button u_ON (.out(ON));
  Button u_D (.out(D));
  Button u_A (.out(A));
  Button u_E (.out(E));
  Button u_B (.out(B));
  Button u_F (.out(F));
  Button u_C (.out(C));
  Button button_3 (.out(Plus));
  Button button_4 (.out(Minus));
  Button button_5 (.out(TImes));
  Button button_6 (.out(Divide));
  or or_17 (or_17_out, NEXT, ON);
  Hex_Digit_Display hex_digit_display_15 (.value(_2[7:4]));  // open: dp
  Hex_Digit_Display hex_digit_display_16 (.value(_2[3:0]));  // open: dp
  // Probe on {D1, D2, D3, D4, D5, D6, D7, D8}
  assign controlled_buffer_31_out = TImes ? 5'b10001 : 5'bz;  // Controlled_Buffer controlled_buffer_31
  or or_18 (or_18_out, TImes, TImes);
  assign controlled_buffer_32_out = TImes ? 5'b01010 : 5'bz;  // Controlled_Buffer controlled_buffer_32
  or or_19 (or_19_out, TImes, TImes);
  assign controlled_buffer_33_out = TImes ? 5'b00100 : 5'bz;  // Controlled_Buffer controlled_buffer_33
  or or_20 (or_20_out, TImes, TImes);
  assign controlled_buffer_34_out = TImes ? 5'b01010 : 5'bz;  // Controlled_Buffer controlled_buffer_34
  or or_21 (or_21_out, TImes, TImes);
  assign controlled_buffer_35_out = TImes ? 5'b10001 : 5'bz;  // Controlled_Buffer controlled_buffer_35
  or or_22 (or_22_out, TImes, TImes);
  DotMatrix #(.matrixrows(5)) dotmatrix_4 (.col0(E1), .col1(E2), .col2(E3), .col3(E4), .col4(E5));
  Hex_Digit_Display hex_digit_display_17 (.value(D1));  // open: dp
  D_Flip_Flop d_ff_1 (.clk(or_17_out), .D(and_1_out), .Q(LED2), .reset(AC));  // open: Qn, preset, en
  D_Flip_Flop d_ff_2 (.clk(or_17_out), .D(and_2_out), .Q(LED1), .preset(AC));  // open: Qn, en, reset
  Register #(.width(5)) register_13 (
    .D(controlled_buffer_31_out), .Q(T1), .clk(or_18_out), .clr(or_23_out));  // open: en
  Register #(.width(5)) register_14 (
    .D(controlled_buffer_32_out), .Q(T2), .clk(or_19_out), .clr(or_23_out));  // open: en
  Register #(.width(5)) register_15 (
    .D(controlled_buffer_33_out), .Q(T3), .clk(or_20_out), .clr(or_23_out));  // open: en
  Register #(.width(5)) register_16 (
    .D(controlled_buffer_34_out), .Q(T4), .clk(or_21_out), .clr(or_23_out));  // open: en
  Register #(.width(5)) register_17 (
    .D(controlled_buffer_35_out), .Q(T5), .clk(or_22_out), .clr(or_23_out));  // open: en
  or or_23 (or_23_out, AC, or_24_out);
  or or_24 (or_24_out, Plus, Minus, Divide);
  Hex_Digit_Display hex_digit_display_18 (.value(D3));  // open: dp
  Hex_Digit_Display hex_digit_display_19 (.value(D2));  // open: dp
  not not_1 (not_1_out, LED2);
  not not_2 (not_2_out, LED2);
  not not_3 (not_3_out, LED1);
  Hex_Digit_Display hex_digit_display_20 (.value(D5));  // open: dp
  Hex_Digit_Display hex_digit_display_21 (.value(D4));  // open: dp
  and and_1 (and_1_out, not_1_out, LED1);
  and and_2 (and_2_out, not_2_out, not_3_out);
  assign controlled_buffer_36_out = Divide ? 5'b00100 : 5'bz;  // Controlled_Buffer controlled_buffer_36
  assign controlled_buffer_37_out = Divide ? 5'b00100 : 5'bz;  // Controlled_Buffer controlled_buffer_37
  assign controlled_buffer_38_out = Divide ? 5'b10101 : 5'bz;  // Controlled_Buffer controlled_buffer_38
  assign controlled_buffer_39_out = Divide ? 5'b00100 : 5'bz;  // Controlled_Buffer controlled_buffer_39
  assign controlled_buffer_40_out = Divide ? 5'b00100 : 5'bz;  // Controlled_Buffer controlled_buffer_40
  Hex_Digit_Display hex_digit_display_22 (.value(D7));  // open: dp
  Hex_Digit_Display hex_digit_display_23 (.value(D6));  // open: dp
  Register #(.width(5)) register_18 (
    .D(controlled_buffer_36_out), .Q(Di1), .clk(or_25_out), .clr(or_29_out));  // open: en
  or or_25 (or_25_out, Divide, Divide);
  Register #(.width(5)) register_19 (
    .D(controlled_buffer_37_out), .Q(Di2), .clk(or_26_out), .clr(or_29_out));  // open: en
  or or_26 (or_26_out, Divide, Divide);
  Register #(.width(5)) register_20 (
    .D(controlled_buffer_38_out), .Q(Di3), .clk(or_27_out), .clr(or_29_out));  // open: en
  or or_27 (or_27_out, Divide, Divide);
  Register #(.width(5)) register_21 (
    .D(controlled_buffer_39_out), .Q(Di4), .clk(or_28_out), .clr(or_29_out));  // open: en
  or or_28 (or_28_out, Divide, Divide);
  Register #(.width(5)) register_22 (
    .D(controlled_buffer_40_out), .Q(Di5), .clk(or_30_out), .clr(or_29_out));  // open: en
  or or_29 (or_29_out, AC, or_31_out);
  or or_30 (or_30_out, Divide, Divide);
  or or_31 (or_31_out, Plus, Minus, TImes);
  Hex_Digit_Display hex_digit_display_24 (.value(D8));  // open: dp
  assign controlled_buffer_41_out = LED2 ? or_9_out : 1'bz;  // Controlled_Buffer controlled_buffer_41
  assign controlled_buffer_42_out = LED1 ? or_9_out : 1'bz;  // Controlled_Buffer controlled_buffer_42
  Shift_Register #(.width(4)) shift_register_1 (
    .in(controlled_buffer_1_out), .clk(controlled_buffer_41_out), .clr(AC), .q0(_2[3:0]), .q1(_2[7:4]),
    .q2(_2[11:8]), .q3(_2[15:12]), .q4(_2[19:16]), .q5(_2[23:20]), .q6(_2[27:24]), .q7(_2[31:28]));  // open: shift, out, load, d0, d1, d2, d3, d4, d5, d6, d7
  Shift_Register #(.width(4)) shift_register_2 (
    .in(controlled_buffer_1_out), .clk(controlled_buffer_42_out), .clr(AC), .q0(_1[3:0]), .q1(_1[7:4]),
    .q2(_1[11:8]), .q3(_1[15:12]), .q4(_1[19:16]), .q5(_1[23:20]), .q6(_1[27:24]), .q7(_1[31:28]));  // open: shift, out, load, d0, d1, d2, d3, d4, d5, d6, d7
  assign controlled_buffer_43_out = tunnel_t_t_t_t ? {5{1'b0}} : 5'bz;  // Controlled_Buffer controlled_buffer_43
  assign controlled_buffer_44_out = tunnel_t_t_t_t ? 5'b01010 : 5'bz;  // Controlled_Buffer controlled_buffer_44
  assign controlled_buffer_45_out = tunnel_t_t_t_t ? 5'b01010 : 5'bz;  // Controlled_Buffer controlled_buffer_45
  assign controlled_buffer_46_out = tunnel_t_t_t_t ? 5'b01010 : 5'bz;  // Controlled_Buffer controlled_buffer_46
  assign controlled_buffer_47_out = tunnel_t_t_t_t ? {5{1'b0}} : 5'bz;  // Controlled_Buffer controlled_buffer_47
  Register #(.width(5)) register_23 (.D(controlled_buffer_43_out), .Q(E1), .clk(or_32_out), .clr(AC));  // open: en
  or or_32 (or_32_out, tunnel_t_t_t_t, tunnel_t_t_t_t);
  Register #(.width(5)) register_24 (.D(controlled_buffer_44_out), .Q(E2), .clk(or_33_out), .clr(AC));  // open: en
  or or_33 (or_33_out, tunnel_t_t_t_t, tunnel_t_t_t_t);
  Register #(.width(5)) register_25 (.D(controlled_buffer_45_out), .Q(E3), .clk(or_34_out), .clr(AC));  // open: en
  or or_34 (or_34_out, tunnel_t_t_t_t, tunnel_t_t_t_t);
  Register #(.width(5)) register_26 (.D(controlled_buffer_46_out), .Q(E4), .clk(or_35_out), .clr(AC));  // open: en
  or or_35 (or_35_out, tunnel_t_t_t_t, tunnel_t_t_t_t);
  Register #(.width(5)) register_27 (.D(controlled_buffer_47_out), .Q(E5), .clk(or_36_out), .clr(AC));  // open: en
  or or_36 (or_36_out, tunnel_t_t_t_t, tunnel_t_t_t_t);
  assign S1 = P1 | M1 | T1 | Di1;  // OR_Gate or_37, 5 bits wide
  assign S2 = P2 | M2 | T2 | Di2;  // OR_Gate or_38, 5 bits wide
  assign S3 = P3 | M3 | T3 | Di3;  // OR_Gate or_39, 5 bits wide
  assign S4 = P4 | M4 | T4 | Di4;  // OR_Gate or_40, 5 bits wide
  assign S5 = P5 | M5 | T5 | Di5;  // OR_Gate or_41, 5 bits wide

  // Other names for the same wires on the sheet: C1[3:0] = _1[3:0]; dec1[31:0] = _1; C2[3:0] = _1[7:4];
  //   C3[3:0] = _1[11:8]; C4[3:0] = _1[15:12]; C5[3:0] = _1[19:16]; C6[3:0] = _1[23:20]; C7[3:0] = _1[27:24];
  //   C8[3:0] = _1[31:28]; C9[3:0] = _2[3:0]; dec2[31:0] = _2; C10[3:0] = _2[7:4]; C11[3:0] = _2[11:8];
  //   C12[3:0] = _2[15:12]; C13[3:0] = _2[19:16]; C14[3:0] = _2[23:20]; C15[3:0] = _2[27:24]; C16[3:0] = _2[31:28];
  //   dec3[31:0] = {D1, D2, D3, D4, D5, D6, D7, D8}; DivideR = Divide; tunnel_t_t_t = Divide; MinusR = Minus;
  //   tunnel_t_t = Minus; PlusR = Plus; tunnel_t = Plus; TimesR = TImes; tunnel = TImes

  // Notes on the sheet:
  //   User Manual:
  //   1. Press ON button once
  //   2. The LED light will light up above Number 1, this means you are entering number on Number 1 slots.
  //   3.  Click NEXT button to enter numbers on Number 2 slot. LED 2 will light up indicating you are entering numbers on Number 2 slots.
  //   4.  Click the Operation button (+, -, *, /) according to the operation you want to the 2 numbers.
  //   5.  Click "=" button to show the answer.
  //   6.  Click the "AC" button to reset the calculator back to zero, so you can enter 2 new numbers to operate.
  //   Hex Number 1
  //   Circuit For Number Operation
  //   Dec Number 1
  //   Digit 2
  //   Hex Number Input Panel
  //   Hex Number 2
  //   Dec Number 2
  //   Circuit For Number Input
  //   Circuit To Display Operator (+, -, *, /)
  //   Dec Result Output
  //   Hex Result Output
endmodule
